# Fritzing sketch sensor-receiver-design (saved by Fritzing 0.9.10b)

parts:
  Part1 = Arduino Uno (Rev3) - ICSP
  Rx1 = mystery part, 4 pins [chip_label=?]

nets:
  N1: Part1.D12/MISO, Rx1.pin3
  N2: Part1.GND, Rx1.pin1
  N3: Part1.5V, Rx1.pin4

notes:
  443MHz receiver
